# Fritzing sketch LDR_Arduino_V001 (saved by Fritzing 0.9.10b)
breadboards: 1

parts:
  U1 = Arduino Uno (Rev3)
  R1 = Resistor [tolerance=±5% power=0.25 resistance=10k package=THT]
  LDR = Photocell (LDR) [package=THT]

nets:
  N1: U1.A0, R1.Pin_0, LDR.pin_1
  N2: U1.GND, R1.Pin_1
  N3: U1.5V, LDR.pin_0
